# Fritzing sketch temp_humd-dht11_3pin (saved by Fritzing 0.9.3b)
breadboards: 1

parts:
  Componente1 = Arduino Uno (Rev3)
  DHT1 = DHT11 Humitidy and Temperature Sensor

nets:
  N1: Componente1.D2, DHT1.VDD
  N2: Componente1.5V, DHT1.DATA
  GND: Componente1.GND, DHT1.GND

custom parts:
  DHT11 Humitidy and Temperature Sensor: DHT11 Humidity and Temperature Sensor
