# Fritzing sketch temperature-ds18b20 (saved by Fritzing 0.9.3b)
breadboards: 1

parts:
  Componente2 = Arduino Uno (Rev3)
  DS1 = DS18B20 1-Wire Temperature Sensor [part_number=DS18B20]

nets:
  GND: Componente2.GND, DS1.GND
  N1: Componente2.D2, DS1.DQ
  5V: Componente2.5V, DS1.VDD
