# Fritzing sketch temperature-tmp36 (saved by Fritzing 0.9.3b)
breadboards: 1

parts:
  Componente2 = Arduino Uno (Rev3)
  T1 = LM35 Temperature Sensor [package="TO92 [THT]"]

nets:
  N1: Componente2.A0, T1.Vout
  N2: Componente2.5V, T1.+Vs
  GND: Componente2.GND, T1.GND
